# Fritzing sketch virtual_piano (saved by Fritzing 0.9.5d)
breadboards: 1

parts:
  Componente1 = Arduino Nano (Rev3.0)
  HC-SR04_Sensor_1 = HC-SR04 Ultrasonic Distance Sensor
  J1 = Piezo Speaker

nets:
  GND: Componente1.GND, HC-SR04_Sensor_1.GND, J1.pin1
  N1: Componente1.D7, J1.pin2
  N2: Componente1.D11/MOSI, HC-SR04_Sensor_1.ECHO
  N3: Componente1.D12/MISO, HC-SR04_Sensor_1.TRIG
  5V: Componente1.5V, HC-SR04_Sensor_1.VCC
